// Logisim project VCVS.circ as structural Verilog: 6 circuits, main circuit main
module main (
  input  [3:0] A_in,
  input  X,
  input  Y,
  input  Z,
  input  I2,
  input  I1,
  input  I0,
  output [3:0] A_register,
  output [3:0] B_register,
  output [3:0] ALU_out
);

  wire and_1_out, and_2_out, and_3_out, not_1_out, not_2_out, not_3_out, not_4_out;
  wire [2:0] register_1_q;

  Register #(.width(3)) register_1 (.D({I2, I1, I0}), .en(1'b1), .clk(X), .Q(register_1_q));  // open: clr
  not not_1 (not_1_out, register_1_q[2]);
  not not_2 (not_2_out, register_1_q[0]);
  not not_3 (not_3_out, register_1_q[1]);
  not not_4 (not_4_out, register_1_q[2]);
  and and_1 (and_1_out, Y, not_1_out);
  and and_2 (and_2_out, not_2_out, not_3_out, register_1_q[2]);
  and and_3 (and_3_out, Z, not_4_out);
  Register #(.width(4)) Reg_A (.D(A_in), .en(1'b1), .clk(and_1_out), .Q(A_register), .clr(and_2_out));
  Register #(.width(4)) Reg_B (.D(ALU_out), .en(1'b1), .clk(and_3_out), .Q(B_register), .clr(and_2_out));
  fourbit_alu fourbit_alu_1 (
    .A(A_register), .B(B_register), .S(register_1_q[1:0]), .alu3(ALU_out[3]), .alu2(ALU_out[2]),
    .alu1(ALU_out[1]), .alu0(ALU_out[0]));  // open: C

  // Notes on the sheet:
  //   000-NOT
  //   001-OR
  //   010-AND
  //   011-ADD
  //   100-CLR
endmodule

module vcvs_register (
  input  clk,
  input  clr,
  input  in0,
  input  in1,
  input  in2,
  input  in3,
  output out0,
  output out1,
  output out2,
  output out3
);

  wire and_1_out, and_2_out, and_3_out, and_4_out, not_1_out;

  not not_1 (not_1_out, clr);
  and and_1 (and_1_out, not_1_out, in0);
  and and_2 (and_2_out, not_1_out, in1);
  and and_3 (and_3_out, not_1_out, in2);
  and and_4 (and_4_out, not_1_out, in3);
  d_flip_flop d_flip_flop_1 (.D(and_1_out), .clk(clk), .Q(out0));  // open: notQ
  d_flip_flop d_flip_flop_2 (.D(and_2_out), .clk(clk), .Q(out1));  // open: notQ
  d_flip_flop d_flip_flop_3 (.D(and_3_out), .clk(clk), .Q(out2));  // open: notQ
  d_flip_flop d_flip_flop_4 (.D(and_4_out), .clk(clk), .Q(out3));  // open: notQ
endmodule

module instruction_register (
  input  clk,
  input  I0,
  input  I1,
  input  I2,
  output IR0,
  output IR1,
  output IR2
);

  d_flip_flop d_flip_flop_1 (.D(I0), .clk(clk), .Q(IR0));  // open: notQ
  d_flip_flop d_flip_flop_2 (.D(I1), .clk(clk), .Q(IR1));  // open: notQ
  d_flip_flop d_flip_flop_3 (.D(I2), .clk(clk), .Q(IR2));  // open: notQ
endmodule

module clocked_sr (
  input  S,
  input  clk,
  input  R,
  output Q,
  output notQ
);

  wire and_1_out, and_2_out;

  and and_1 (and_1_out, S, clk);
  and and_2 (and_2_out, clk, R);
  nor nor_1 (notQ, and_1_out, Q);
  nor nor_2 (Q, notQ, and_2_out);
endmodule

module d_latch (
  input  D,
  input  clk,
  output Q,
  output notQ
);

  wire not_1_out;

  not not_1 (not_1_out, D);
  clocked_sr clocked_sr_1 (.S(D), .clk(clk), .R(not_1_out), .Q(Q), .notQ(notQ));
endmodule

module d_flip_flop (
  input  D,
  input  clk,
  output Q,
  output notQ
);

  wire d_latch_1_notq, d_latch_1_q, not_1_out;

  not not_1 (not_1_out, clk);
  d_latch d_latch_1 (.D(D), .clk(clk), .Q(d_latch_1_q), .notQ(d_latch_1_notq));
  clocked_sr clocked_sr_1 (.S(d_latch_1_q), .clk(not_1_out), .R(d_latch_1_notq), .Q(Q), .notQ(notQ));
endmodule
